# Fritzing sketch StacjaPogodowaWiring (saved by Fritzing 0.9.3b)
breadboards: 1

parts:
  Pico_H1 = Raspberry Pi Pico H
  DHT1 = DHT22 Humidity and Temperature Sensor
  LCD2 = LCD screen
  LCM1602_IIC2 = LCM1602 IIC [part_number="LCM1602 IIC" chip_label="LCM1602 IIC" package="DIP (Dual Inline) [THT]"]
  IR1 = TSOP312.., 314.. [package=THT]

nets:
  N1: Pico_H1.VBUS, LCM1602_IIC2.VCC
  GND: Pico_H1.GND, DHT1.GND, LCM1602_IIC2.GND, IR1.GND
  3V3: Pico_H1.3V3, DHT1.VDD, IR1.Vs
  N2: Pico_H1.GP17, DHT1.DATA
  N3: Pico_H1.GP16, IR1.Data
  N4: Pico_H1.GP1, LCM1602_IIC2.SCL
  N5: Pico_H1.GP0, LCM1602_IIC2.SDA
  VSS: LCD2.VSS, LCM1602_IIC2.VSS
  VDD: LCD2.VDD, LCM1602_IIC2.VDD
  N6: LCD2.V0, LCM1602_IIC2.V0
  N7: LCD2.RS, LCM1602_IIC2.RS
  N8: LCD2.R/W, LCM1602_IIC2.RW
  N9: LCD2.E, LCM1602_IIC2.E
  N10: LCD2.DB0, LCM1602_IIC2.D0
  N11: LCD2.DB1, LCM1602_IIC2.D1
  N12: LCD2.DB2, LCM1602_IIC2.D2
  N13: LCD2.DB3, LCM1602_IIC2.D3
  N14: LCD2.DB4, LCM1602_IIC2.D4
  N15: LCD2.DB5, LCM1602_IIC2.D5
  N16: LCD2.DB6, LCM1602_IIC2.D6
  N17: LCD2.DB7, LCM1602_IIC2.D7
  N18: LCD2.LED+, LCM1602_IIC2.A
  N19: LCD2.LED-, LCM1602_IIC2.K
  N20: LCM1602_IIC2.LED_A, LCM1602_IIC2.LED_B

custom parts:
  Raspberry Pi Pico H: Raspberry Pi Pico H. Based around the RP2040 microcontroller the Pico H is a low cost microcontroller device bringing Raspberry Pi quality, cost, and easy of use to the microcontroller space.
  LCM1602 IIC: I2C-Module to use a 1602 or 2004 LCD on with the wire.h libory Serial LCD Modul
